// Logisim project main_v1.circ as structural Verilog: 9 circuits, main circuit main
module main (
  input  in_1,
  input  [7:0] in_2,
  output [7:0] out_3,
  output [15:0] out_4
);

  wire alu_1_out_7, clock_1_out, not_1_out, transistor_1_out, undriven;
  wire [2:0] counter_1_q;
  wire [3:0] n8_bit_splitter_2_left, n8_bit_splitter_3_right, program_counter_1_o_rw, register_1_out_6;
  wire [6:0] ins_merger_1_out_3;
  wire [7:0] alu_1_out_5, register_1_out_5, register_2_out_5, register_2_out_6, register_4_out_5,
       register_5_out_5;
  wire [7:4] register_1_out_6_2;

  Clock clock_1 (.out(clock_1_out));
  Transistor transistor_1 (.in(clock_1_out), .out(transistor_1_out), .gate(out_4[15]));
  Register register_1 (
    .CLK(transistor_1_out), .L(out_4[9]), .out_6({register_1_out_6_2, register_1_out_6}), .E(out_4[8]),
    .in_4({register_1_out_6_2, register_1_out_6}), .out_5(register_1_out_5));
  _8_bit_Splitter u_8_bit_splitter_1 (.in_1(register_2_out_6), .RIGHT(register_1_out_6));  // open: LEFT
  Program_Counter program_counter_1 (
    .L(out_4[1]), .in_3(register_1_out_6), .CE(out_4[3]), .out_6(register_1_out_6),
    .O_RW(program_counter_1_o_rw), .E(out_4[2]), .CLK(transistor_1_out));
  LED led_1 (.in(register_1_out_5[4]));
  LED led_2 (.in(register_1_out_5[6]));
  LED led_3 (.in(register_1_out_5[7]));
  LED led_4 (.in(register_1_out_5[5]));
  Register register_2 (
    .CLK(transistor_1_out), .L(out_4[10]), .out_6(register_2_out_6), .E(out_4[11]),
    .in_4({register_1_out_6_2, register_1_out_6}), .out_5(register_2_out_5));
  LED led_5 (.in(register_2_out_5[6]));
  LED led_6 (.in(register_2_out_5[7]));
  LED led_7 (.in(program_counter_1_o_rw[3]));
  LED led_8 (.in(program_counter_1_o_rw[2]));
  LED led_9 (.in(program_counter_1_o_rw[1]));
  LED led_10 (.in(register_1_out_5[1]));
  LED led_11 (.in(register_1_out_5[0]));
  LED led_12 (.in(register_1_out_5[2]));
  LED led_13 (.in(register_1_out_5[3]));
  LED led_14 (.in(register_2_out_5[5]));
  LED led_15 (.in(register_2_out_5[3]));
  LED led_16 (.in(register_2_out_5[2]));
  LED led_17 (.in(register_2_out_5[4]));
  _8_bit_Splitter u_8_bit_splitter_2 (.in_1(register_2_out_5), .LEFT(n8_bit_splitter_2_left));  // open: RIGHT
  LED led_18 (.in(program_counter_1_o_rw[0]));
  LED led_19 (.in(register_2_out_5[0]));
  LED led_20 (.in(register_2_out_5[1]));
  ALU alu_1 (
    .SU(out_4[6]), .in_2(register_1_out_5), .out_6({register_1_out_6_2, register_1_out_6}),
    .in_4(register_5_out_5), .EO(out_4[7]), .out_5(alu_1_out_5), .out_7(alu_1_out_7));
  Register register_3 (
    .CLK(transistor_1_out), .L(out_4[4]), .in_4({register_1_out_6_2, register_1_out_6}), .out_5(out_3));  // open: out_6, E
  LED led_21 (.in(alu_1_out_5[7]));
  LED led_22 (.in(alu_1_out_5[4]));
  LED led_23 (.in(alu_1_out_5[5]));
  LED led_24 (.in(alu_1_out_5[6]));
  Register register_4 (
    .CLK(transistor_1_out), .L(out_4[14]), .in_4({register_1_out_6_2, register_1_out_6}),
    .out_5(register_4_out_5));  // open: out_6, E
  LED led_25 (.in(alu_1_out_5[0]));
  LED led_26 (.in(alu_1_out_5[1]));
  LED led_27 (.in(alu_1_out_5[3]));
  LED led_28 (.in(alu_1_out_5[2]));
  _8_bit_Splitter u_8_bit_splitter_3 (.in_1(register_4_out_5), .RIGHT(n8_bit_splitter_3_right));  // open: LEFT
  LED led_29 (.in(n8_bit_splitter_3_right[3]));
  LED led_30 (.in(n8_bit_splitter_3_right[2]));
  Counter #(.width(3), .max('h7)) counter_1 (.Q(counter_1_q), .clk(not_1_out));  // open: load, D, count, carry, clr
  not not_1 (not_1_out, transistor_1_out);
  LED led_31 (.in(n8_bit_splitter_3_right[1]));
  LED led_32 (.in(n8_bit_splitter_3_right[0]));
  Ins_Merger ins_merger_1 (.STEP(counter_1_q), .INS(n8_bit_splitter_2_left), .out_3(ins_merger_1_out_3));
  Register register_5 (
    .CLK(transistor_1_out), .L(out_4[5]), .E(undriven), .in_4({register_1_out_6_2, register_1_out_6}),
    .out_5(register_5_out_5));  // open: out_6
  LED led_33 (.in(register_5_out_5[6]));
  LED led_34 (.in(register_5_out_5[7]));
  RAM #(.addrWidth(4), .bus("separate")) ram_1 (
    .addr(n8_bit_splitter_3_right), .din({register_1_out_6_2, register_1_out_6}),
    .data({register_1_out_6_2, register_1_out_6}), .str(out_4[13]), .clk(transistor_1_out), .ld(out_4[12]));  // open: sel, clr
  LED led_35 (.in(register_5_out_5[3]));
  LED led_36 (.in(register_5_out_5[5]));
  LED led_37 (.in(register_5_out_5[2]));
  LED led_38 (.in(register_5_out_5[4]));
  ROM #(.addrWidth(7), .dataWidth(16)) rom_1 (.addr(ins_merger_1_out_3), .data(out_4));  // open: sel
  LED led_39 (.in(register_5_out_5[1]));
  LED led_40 (.in(register_5_out_5[0]));
  Transistor #(.\type ("n"), .width(8)) transistor_2 (
    .in(in_2), .out({register_1_out_6_2, register_1_out_6}), .gate(in_1));
  LED led_41 (.in(register_1_out_6_2[6]));
  LED led_42 (.in(register_1_out_6_2[7]));
  LED led_43 (.in(register_1_out_6_2[4]));
  LED led_44 (.in(register_1_out_6_2[5]));
  LED led_45 (.in(register_1_out_6[3]));
  LED led_46 (.in(register_1_out_6[2]));
  LED led_47 (.in(register_1_out_6[1]));
  LED led_48 (.in(register_1_out_6[0]));

  // Other names for the same wires on the sheet: J = out_4[1]; CO = out_4[2]; CE = out_4[3]; OI = out_4[4];
  //   BI = out_4[5]; SU = out_4[6]; EO = out_4[7]; AO = out_4[8]; AI = out_4[9]; II = out_4[10]; IO = out_4[11];
  //   RO = out_4[12]; RI = out_4[13]; MI = out_4[14]; HLT = out_4[15]

  // Notes on the sheet:
  //   A-REG
  //   INS-REG
  //   OI
  //   OUTPUT
  //   MEM-ADDR
  //   B-REG
  //   RAM
  //   contents of rom_1 (hex, n*v repeats v):
  //   4004 1408 6*0 4004 1408 4800 1200 4*0 4004 1408 4800 1020 280 0 0 0 4004 1408 6*0 4004 1408 6*0 4004
  //   1408 6*0 4004 1408 6*0 4004 1408 6*0 4004 1408 6*0 4004 1408 6*0 4004 1408 6*0 4004 1408 6*0 4004
  //   1408 6*0 4004 1408 6*0 4004 1408 110 5*0 4004 1408 8000
endmodule

module D_Latch (
  input  in_1,
  input  in_2,
  output q,
  output nq
);

  wire nand_1_out, nand_2_out;

  nand nand_1 (nand_1_out, in_1, in_2);
  nand nand_2 (nand_2_out, nand_1_out, in_2);
  nand nand_3 (q, nand_1_out, nq);
  nand nand_4 (nq, q, nand_2_out);
endmodule

module Register (
  input  CLK,
  input  E,
  input  L,
  input  [7:0] in_4,
  output [7:0] out_5,
  output [7:0] out_6
);

  wire and_1_out, and_2_out, and_3_out, and_4_out, and_5_out, and_6_out, and_7_out, and_8_out, and_9_out,
       and_10_out, and_11_out, and_12_out, and_13_out, and_14_out, and_15_out, and_16_out, not_1_out,
       not_2_out, not_3_out, not_4_out, not_5_out, not_6_out, not_7_out, not_8_out, or_1_out, or_2_out,
       or_3_out, or_4_out, or_5_out, or_6_out, or_7_out, or_8_out;

  not not_1 (not_1_out, L);
  not not_2 (not_2_out, L);
  not not_3 (not_3_out, L);
  not not_4 (not_4_out, L);
  not not_5 (not_5_out, L);
  not not_6 (not_6_out, L);
  not not_7 (not_7_out, L);
  not not_8 (not_8_out, L);
  and and_1 (and_1_out, out_5[0], not_1_out);
  and and_2 (and_2_out, L, in_4[0]);
  and and_3 (and_3_out, out_5[1], not_2_out);
  and and_4 (and_4_out, L, in_4[1]);
  and and_5 (and_5_out, out_5[2], not_3_out);
  and and_6 (and_6_out, L, in_4[2]);
  and and_7 (and_7_out, out_5[3], not_4_out);
  and and_8 (and_8_out, L, in_4[3]);
  and and_9 (and_9_out, out_5[4], not_5_out);
  and and_10 (and_10_out, L, in_4[4]);
  and and_11 (and_11_out, out_5[5], not_6_out);
  and and_12 (and_12_out, L, in_4[5]);
  and and_13 (and_13_out, out_5[6], not_7_out);
  and and_14 (and_14_out, L, in_4[6]);
  and and_15 (and_15_out, out_5[7], not_8_out);
  and and_16 (and_16_out, L, in_4[7]);
  or or_1 (or_1_out, and_1_out, and_2_out);
  or or_2 (or_2_out, and_3_out, and_4_out);
  or or_3 (or_3_out, and_5_out, and_6_out);
  or or_4 (or_4_out, and_7_out, and_8_out);
  or or_5 (or_5_out, and_9_out, and_10_out);
  or or_6 (or_6_out, and_11_out, and_12_out);
  or or_7 (or_7_out, and_13_out, and_14_out);
  or or_8 (or_8_out, and_15_out, and_16_out);
  D_Flip_Flop_part d_ff_1 (.clk(CLK), .D(or_1_out), .Q(out_5[0]));  // open: Qn, preset, en, reset
  D_Flip_Flop_part d_ff_2 (.clk(CLK), .D(or_2_out), .Q(out_5[1]));  // open: Qn, preset, en, reset
  D_Flip_Flop_part d_ff_3 (.clk(CLK), .D(or_3_out), .Q(out_5[2]));  // open: Qn, preset, en, reset
  D_Flip_Flop_part d_ff_4 (.clk(CLK), .D(or_4_out), .Q(out_5[3]));  // open: Qn, preset, en, reset
  D_Flip_Flop_part d_ff_5 (.clk(CLK), .D(or_5_out), .Q(out_5[4]));  // open: Qn, preset, en, reset
  D_Flip_Flop_part d_ff_6 (.clk(CLK), .D(or_6_out), .Q(out_5[5]));  // open: Qn, preset, en, reset
  D_Flip_Flop_part d_ff_7 (.clk(CLK), .D(or_7_out), .Q(out_5[6]));  // open: Qn, preset, en, reset
  D_Flip_Flop_part d_ff_8 (.clk(CLK), .D(or_8_out), .Q(out_5[7]));  // open: Qn, preset, en, reset
  assign out_6 = E ? out_5 : 8'bz;  // Controlled_Buffer controlled_buffer_1

  // Notes on the sheet:
  //   D1
endmodule

module ALU (
  input  SU,
  input  [7:0] in_2,
  input  EO,
  input  [7:0] in_4,
  output [7:0] out_5,
  output [7:0] out_6,
  output out_7
);

  wire [7:0] xor_7_out;

  xor xor_1 (xor_7_out[7], in_4[7], SU);
  xor xor_2 (xor_7_out[6], in_4[6], SU);
  xor xor_3 (xor_7_out[5], in_4[5], SU);
  xor xor_4 (xor_7_out[4], in_4[4], SU);
  assign out_6 = EO ? out_5 : 8'bz;  // Controlled_Buffer controlled_buffer_1
  Adder adder_1 (.a(in_2), .b(xor_7_out), .out(out_5), .cin(SU), .cout(out_7));
  xor xor_5 (xor_7_out[3], in_4[3], SU);
  xor xor_6 (xor_7_out[2], in_4[2], SU);
  xor xor_7 (xor_7_out[0], in_4[0], SU);
  xor xor_8 (xor_7_out[1], in_4[1], SU);

  // Notes on the sheet:
  //   A
  //   B
endmodule

module D_Flip_Flop (
  input  in_1,
  input  in_2,
  output out_3,
  output out_4
);

  wire edge_trigger_1_out_2;

  Edge_Trigger edge_trigger_1 (.in_1(in_1), .out_2(edge_trigger_1_out_2));
  D_Latch d_latch_1 (.in_1(in_2), .q(out_3), .in_2(edge_trigger_1_out_2), .nq(out_4));
endmodule

module Edge_Trigger (
  input  in_1,
  output out_2
);

  wire not_1_out, not_2_out, not_3_out;

  not not_1 (not_1_out, not_2_out);
  not not_2 (not_2_out, not_3_out);
  not not_3 (not_3_out, in_1);
  and and_1 (out_2, in_1, not_1_out);
endmodule

module Program_Counter (
  input  E,
  input  L,
  input  [3:0] in_3,
  input  CE,
  input  CLK,
  output [3:0] out_6,
  output [3:0] O_RW
);

  Counter #(.width(4), .max('hf)) counter_1 (.load(L), .D(in_3), .count(CE), .Q(O_RW), .clk(CLK));  // open: carry, clr
  assign out_6 = E ? O_RW : 4'bz;  // Controlled_Buffer controlled_buffer_1
endmodule

module _8_bit_Splitter (
  input  [7:0] in_1,
  output [3:0] RIGHT,
  output [3:0] LEFT
);


  assign LEFT = in_1[7:4];
  assign RIGHT = in_1[3:0];
endmodule

module Ins_Merger (
  input  [2:0] STEP,
  input  [3:0] INS,
  output [6:0] out_3
);


  assign out_3 = {INS, STEP};
endmodule
