// Logisim project main_v4.circ as structural Verilog: 12 circuits, main circuit main
module main (
  output [1:0] Flags_Register,
  output [7:0] A_Register,
  output [7:0] Sum_Register,
  output [7:0] B_Register,
  output [7:0] out_5,
  output [7:0] out_6,
  output [3:0] out_7,
  output [8:0] out_8,
  output [2:0] out_9,
  output [3:0] Program_Counter,
  output [7:0] Output_Register
);

  wire AI, AO, BI, CE, CLK, clock_1_out, CO, EO, FI, HLT, II, IO, J, MI, OI, RI, RO, SU;
  wire [1:0] n8_bit_nor_1_out_2;
  wire [3:0] n8_bit_splitter_2_left;
  wire [7:0] register_2_out_5, register_5_out_6;

  Register register_1 (.CLK(CLK), .L(AI), .out_6(out_5), .E(AO), .in_4(out_5), .out_5(A_Register));
  Register register_2 (.CLK(CLK), .L(MI), .in_4(out_5), .out_5(register_2_out_5));  // open: out_6, E
  Program_Counter program_counter_1 (
    .L(J), .in_3(out_5[3:0]), .CE(CE), .out_6(out_5[3:0]), .O_RW(Program_Counter), .E(CO), .CLK(CLK));
  _8_bit_Splitter u_8_bit_splitter_1 (.in_1(register_2_out_5), .RIGHT(out_7));  // open: LEFT
  ALU alu_1 (
    .in_1(A_Register), .SU(SU), .in_3(B_Register), .CY(n8_bit_nor_1_out_2[1]), .out_6(out_5), .EO(EO),
    .out_5(Sum_Register));
  _8_Bit_NOR u_8_bit_nor_1 (.in_1(Sum_Register), .out_2(n8_bit_nor_1_out_2[0]));
  RAM #(.addrWidth(4), .bus("separate")) ram_1 (
    .addr(out_7), .din(out_5), .data(out_5), .str(RI), .clk(CLK), .ld(RO));  // open: sel, clr
  Register register_3 (.CLK(CLK), .L(OI), .in_4(out_5), .out_5(Output_Register));  // open: out_6, E
  Register_part #(.width(2)) register_4 (.D(n8_bit_nor_1_out_2), .en(FI), .Q(Flags_Register), .clk(CLK));  // open: clr
  Clock clock_1 (.out(clock_1_out));
  Transistor transistor_1 (.in(clock_1_out), .out(CLK), .gate(HLT));
  Register register_5 (.CLK(CLK), .L(II), .out_6(register_5_out_6), .E(IO), .in_4(out_5), .out_5(out_6));
  Instruction_Counter instruction_counter_1 (.out_2(out_9), .in_1(CLK));
  _8_bit_Splitter u_8_bit_splitter_2 (.in_1(out_6), .LEFT(n8_bit_splitter_2_left));  // open: RIGHT
  Ins_Merger ins_merger_1 (.FLAGS(out_9), .STEP(n8_bit_splitter_2_left), .out_4(out_8), .in_3(Flags_Register));
  Register register_6 (.CLK(CLK), .L(BI), .in_4(out_5), .out_5(B_Register));  // open: out_6, E
  _8_bit_Splitter u_8_bit_splitter_3 (.in_1(register_5_out_6), .RIGHT(out_5[3:0]));  // open: LEFT
  ROM #(.addrWidth(9), .dataWidth(16)) rom_1 (
    .addr(out_8), .data({HLT, MI, RI, RO, IO, II, AI, AO, EO, SU, BI, OI, CE, CO, J, FI}));  // open: sel

  // Other names for the same wires on the sheet: FLAGS[1:0] = Flags_Register

  // Notes on the sheet:
  //   Memory Address Register
  //   Memory
  //   Clock
  //   Instruction Register
  //   logic signal addr.
  //   Bus
  //   ⭐⭐⭐Control Unit⭐⭐⭐
  //   ROM (opcode logic)
  //   contents of rom_1 (hex, n*v repeats v):
  //   4*4004 4*1408 24*0 4*4004 4*1408 4*4800 4*1200 16*0 4*4004 4*1408 4*4800 4*1020 4*281 12*0 4*4004
  //   4*1408 4*4800 4*1020 4*2c1 12*0 4*4004 4*1408 4*4800 4*2100 16*0 4*4004 4*1408 4*a00 20*0 4*4004
  //   4*1408 4*110 20*0 4*4004 4*1408 4*802 20*0 4*4004 4*1408 0 802 0 802 20*0 4*4004 4*1408 0 0 802 802
  //   20*0 4*4004 4*1408 4*8000 20*0 4*4004 4*1408 4*4800 4*1010 4*8000
endmodule

module D_Latch (
  input  in_1,
  input  in_2,
  output q,
  output nq
);

  wire nand_1_out, nand_2_out;

  nand nand_1 (nand_1_out, in_1, in_2);
  nand nand_2 (nand_2_out, nand_1_out, in_2);
  nand nand_3 (q, nand_1_out, nq);
  nand nand_4 (nq, q, nand_2_out);
endmodule

module Register (
  input  CLK,
  input  E,
  input  L,
  input  [7:0] in_4,
  output [7:0] out_5,
  output [7:0] out_6
);

  wire and_1_out, and_2_out, and_3_out, and_4_out, and_5_out, and_6_out, and_7_out, and_8_out, and_9_out,
       and_10_out, and_11_out, and_12_out, and_13_out, and_14_out, and_15_out, and_16_out, not_1_out,
       not_2_out, not_3_out, not_4_out, not_5_out, not_6_out, not_7_out, not_8_out, or_1_out, or_2_out,
       or_3_out, or_4_out, or_5_out, or_6_out, or_7_out, or_8_out;

  not not_1 (not_1_out, L);
  not not_2 (not_2_out, L);
  not not_3 (not_3_out, L);
  not not_4 (not_4_out, L);
  not not_5 (not_5_out, L);
  not not_6 (not_6_out, L);
  not not_7 (not_7_out, L);
  not not_8 (not_8_out, L);
  and and_1 (and_1_out, out_5[0], not_1_out);
  and and_2 (and_2_out, L, in_4[0]);
  and and_3 (and_3_out, out_5[1], not_2_out);
  and and_4 (and_4_out, L, in_4[1]);
  and and_5 (and_5_out, out_5[2], not_3_out);
  and and_6 (and_6_out, L, in_4[2]);
  and and_7 (and_7_out, out_5[3], not_4_out);
  and and_8 (and_8_out, L, in_4[3]);
  and and_9 (and_9_out, out_5[4], not_5_out);
  and and_10 (and_10_out, L, in_4[4]);
  and and_11 (and_11_out, out_5[5], not_6_out);
  and and_12 (and_12_out, L, in_4[5]);
  and and_13 (and_13_out, out_5[6], not_7_out);
  and and_14 (and_14_out, L, in_4[6]);
  and and_15 (and_15_out, out_5[7], not_8_out);
  and and_16 (and_16_out, L, in_4[7]);
  or or_1 (or_1_out, and_1_out, and_2_out);
  or or_2 (or_2_out, and_3_out, and_4_out);
  or or_3 (or_3_out, and_5_out, and_6_out);
  or or_4 (or_4_out, and_7_out, and_8_out);
  or or_5 (or_5_out, and_9_out, and_10_out);
  or or_6 (or_6_out, and_11_out, and_12_out);
  or or_7 (or_7_out, and_13_out, and_14_out);
  or or_8 (or_8_out, and_15_out, and_16_out);
  D_Flip_Flop_part d_ff_1 (.clk(CLK), .D(or_1_out), .Q(out_5[0]));  // open: Qn, preset, en, reset
  D_Flip_Flop_part d_ff_2 (.clk(CLK), .D(or_2_out), .Q(out_5[1]));  // open: Qn, preset, en, reset
  D_Flip_Flop_part d_ff_3 (.clk(CLK), .D(or_3_out), .Q(out_5[2]));  // open: Qn, preset, en, reset
  D_Flip_Flop_part d_ff_4 (.clk(CLK), .D(or_4_out), .Q(out_5[3]));  // open: Qn, preset, en, reset
  D_Flip_Flop_part d_ff_5 (.clk(CLK), .D(or_5_out), .Q(out_5[4]));  // open: Qn, preset, en, reset
  D_Flip_Flop_part d_ff_6 (.clk(CLK), .D(or_6_out), .Q(out_5[5]));  // open: Qn, preset, en, reset
  D_Flip_Flop_part d_ff_7 (.clk(CLK), .D(or_7_out), .Q(out_5[6]));  // open: Qn, preset, en, reset
  D_Flip_Flop_part d_ff_8 (.clk(CLK), .D(or_8_out), .Q(out_5[7]));  // open: Qn, preset, en, reset
  assign out_6 = E ? out_5 : 8'bz;  // Controlled_Buffer controlled_buffer_1

  // Notes on the sheet:
  //   D1
endmodule

module ALU (
  input  [7:0] in_1,
  input  EO,
  input  [7:0] in_3,
  input  SU,
  output [7:0] out_5,
  output [7:0] out_6,
  output CY
);

  wire adder_1_cout, subtractor_1_bout;
  wire [7:0] adder_1_out, subtractor_1_out;

  Adder adder_1 (.a(in_1), .b(in_3), .out(adder_1_out), .cout(adder_1_cout));  // open: cin
  Subtractor subtractor_1 (.a(in_1), .b(in_3), .out(subtractor_1_out), .bout(subtractor_1_bout));  // open: bin
  Multiplexer #(.width(8)) multiplexer_1 (.in0(adder_1_out), .in1(subtractor_1_out), .out(out_5), .sel(SU), .en(1'b1));
  Multiplexer multiplexer_2 (.in0(adder_1_cout), .in1(subtractor_1_bout), .out(CY), .sel(SU), .en(1'b1));
  assign out_6 = EO ? out_5 : 8'bz;  // Controlled_Buffer controlled_buffer_1

  // Notes on the sheet:
  //   A
  //   B
endmodule

module D_Flip_Flop (
  input  in_1,
  input  in_2,
  output out_3,
  output out_4
);

  wire edge_trigger_1_out_2;

  Edge_Trigger edge_trigger_1 (.in_1(in_1), .out_2(edge_trigger_1_out_2));
  D_Latch d_latch_1 (.in_1(in_2), .q(out_3), .in_2(edge_trigger_1_out_2), .nq(out_4));
endmodule

module Edge_Trigger (
  input  in_1,
  output out_2
);

  wire not_1_out, not_2_out, not_3_out;

  not not_1 (not_1_out, not_3_out);
  not not_2 (not_2_out, in_1);
  not not_3 (not_3_out, not_2_out);
  and and_1 (out_2, in_1, not_1_out);
endmodule

module Program_Counter (
  input  E,
  input  L,
  input  [3:0] in_3,
  input  CE,
  input  CLK,
  output [3:0] out_6,
  output [3:0] O_RW
);

  Counter #(.width(4), .max('hf)) counter_1 (.load(L), .D(in_3), .count(CE), .Q(O_RW), .clk(CLK));  // open: carry, clr
  assign out_6 = E ? O_RW : 4'bz;  // Controlled_Buffer controlled_buffer_1
endmodule

module _8_bit_Splitter (
  input  [7:0] in_1,
  output [3:0] RIGHT,
  output [3:0] LEFT
);


  assign LEFT = in_1[7:4];
  assign RIGHT = in_1[3:0];
endmodule

module Ins_Merger (
  input  [3:0] STEP,
  input  [2:0] FLAGS,
  input  [1:0] in_3,
  output [8:0] out_4
);


  assign out_4 = {STEP, FLAGS, in_3};

  // Notes on the sheet:
  //   INS
endmodule

module Instruction_Counter (
  input  in_1,
  output [2:0] out_2
);

  wire not_1_out;

  not not_1 (not_1_out, in_1);
  Counter #(.width(3), .max('h7)) counter_1 (.Q(out_2), .clk(not_1_out));  // open: load, D, count, carry, clr
endmodule

module _8_Bit_NOR (
  input  [7:0] in_1,
  output out_2
);

  nor nor_1 (out_2, in_1[0], in_1[1], in_1[2], in_1[3], in_1[4], in_1[5], in_1[6], in_1[7]);
endmodule

module exp (
  input  in_1,
  input  [7:0] in_2,
  input  in_3,
  input  [7:0] in_4,
  output [7:0] out_5
);

  wire adder_1_cout;
  wire [7:0] xor_8_out;

  xor xor_1 (xor_8_out[7], in_4[7], in_3);
  xor xor_2 (xor_8_out[6], in_4[6], in_3);
  xor xor_3 (xor_8_out[5], in_4[5], in_3);
  xor xor_4 (xor_8_out[4], in_4[4], in_3);
  Adder adder_1 (.a(in_2), .b(xor_8_out), .out(out_5), .cin(in_1), .cout(adder_1_cout));
  xor xor_5 (xor_8_out[3], in_4[3], in_3);
  xor xor_6 (xor_8_out[2], in_4[2], in_3);
  xor xor_7 (xor_8_out[1], in_4[1], in_3);
  xor xor_8 (xor_8_out[0], in_4[0], in_3);

  // Notes on the sheet:
  //   one's complement
endmodule
